# Fritzing sketch 1 (saved by Fritzing 0.9.10b)
breadboards: 1

parts:
  Componente1 = Arduino Uno (Rev3) - ICSP
  LED1 = smd LED [color="Red (633nm)" package="0805 [SMD]"]

nets:
  N1: Componente1.5V, LED1.anode
  N2: Componente1.GND, LED1.cathode
